// Logisim project Main.circ as structural Verilog: 6 circuits, main circuit main
module main (
);

  wire clock_1_out, RESET_IP_out;
  wire [7:0] adder_1_out, IP_q, ula_1_res;
  wire [23:0] MI_data;
  wire [31:0] bancoreg_1_o1, bancoreg_1_o2;
  wire [31:8] ula_1_res_2;

  Clock clock_1 (.out(clock_1_out));
  Register IP (.D(adder_1_out), .en(1'b1), .clk(clock_1_out), .Q(IP_q), .clr(RESET_IP_out));
  Adder adder_1 (.a(8'h1), .b(IP_q), .out(adder_1_out));  // open: cin, cout
  Button RESET_IP (.out(RESET_IP_out));
  ROM #(.dataWidth(24)) MI (.addr(IP_q), .data(MI_data));
  BancoReg bancoreg_1 (
    .CLK(clock_1_out), .D({ula_1_res_2, ula_1_res}), .RS1(MI_data[15:11]), .RS2(MI_data[20:16]),
    .RD(MI_data[7:3]), .O1(bancoreg_1_o1), .O2(bancoreg_1_o2));  // open: W
  ULA ula_1 (.OP1(bancoreg_1_o1), .OP2(bancoreg_1_o2), .RES({ula_1_res_2, ula_1_res}));  // open: OPR
  RAM #(.dataWidth(32), .enables("line")) MD (.addr(ula_1_res), .clk(clock_1_out));  // open: we, din, dout
endmodule

module BancoReg (
  input  CLK,
  input  [31:0] D,
  input  [4:0] RS1,
  input  [4:0] RS2,
  input  [4:0] RD,
  input  W,
  output [31:0] O1,
  output [31:0] O2
);

  wire demultiplexer_1_out0, demultiplexer_1_out1, demultiplexer_1_out2, demultiplexer_1_out3,
       demultiplexer_1_out4, demultiplexer_1_out5, demultiplexer_1_out6, demultiplexer_1_out7,
       demultiplexer_1_out8, demultiplexer_1_out9, demultiplexer_1_out10, demultiplexer_1_out11,
       demultiplexer_1_out12, demultiplexer_1_out13, demultiplexer_1_out14, demultiplexer_1_out15,
       demultiplexer_1_out16, demultiplexer_1_out17, demultiplexer_1_out18, demultiplexer_1_out19,
       demultiplexer_1_out20, demultiplexer_1_out21, demultiplexer_1_out22, demultiplexer_1_out23,
       demultiplexer_1_out24, demultiplexer_1_out25, demultiplexer_1_out26, demultiplexer_1_out27,
       demultiplexer_1_out28, demultiplexer_1_out29, demultiplexer_1_out30, demultiplexer_1_out31;
  wire [31:0] register_1_q, register_2_q, register_3_q, register_4_q, register_5_q, register_6_q,
       register_7_q, register_8_q, register_9_q, register_10_q, register_11_q, register_12_q, register_13_q,
       register_14_q, register_15_q, register_16_q, register_17_q, register_18_q, register_19_q,
       register_20_q, register_21_q, register_22_q, register_23_q, register_24_q, register_25_q,
       register_26_q, register_27_q, register_28_q, register_29_q, register_30_q, register_31_q,
       register_32_q;

  ULA ula_1 ();  // open: OPR, OP1, OP2, RES
  Demultiplexer #(.select(5)) demultiplexer_1 (
    .out0(demultiplexer_1_out0), .out1(demultiplexer_1_out1), .out2(demultiplexer_1_out2),
    .out3(demultiplexer_1_out3), .out4(demultiplexer_1_out4), .out5(demultiplexer_1_out5),
    .out6(demultiplexer_1_out6), .out7(demultiplexer_1_out7), .out8(demultiplexer_1_out8),
    .out9(demultiplexer_1_out9), .out10(demultiplexer_1_out10), .out11(demultiplexer_1_out11),
    .out12(demultiplexer_1_out12), .out13(demultiplexer_1_out13), .out14(demultiplexer_1_out14),
    .out15(demultiplexer_1_out15), .out16(demultiplexer_1_out16), .out17(demultiplexer_1_out17),
    .out18(demultiplexer_1_out18), .out19(demultiplexer_1_out19), .out20(demultiplexer_1_out20),
    .out21(demultiplexer_1_out21), .out22(demultiplexer_1_out22), .out23(demultiplexer_1_out23),
    .out24(demultiplexer_1_out24), .out25(demultiplexer_1_out25), .out26(demultiplexer_1_out26),
    .out27(demultiplexer_1_out27), .out28(demultiplexer_1_out28), .out29(demultiplexer_1_out29),
    .out30(demultiplexer_1_out30), .out31(demultiplexer_1_out31), .in(W), .sel(RD));
  Register #(.width(32)) register_1 (.D(D), .en(demultiplexer_1_out0), .clk(CLK), .Q(register_1_q), .clr(1'b1));
  Register #(.width(32)) register_2 (.D(D), .en(demultiplexer_1_out1), .clk(CLK), .Q(register_2_q));  // open: clr
  Register #(.width(32)) register_3 (.D(D), .en(demultiplexer_1_out2), .clk(CLK), .Q(register_3_q));  // open: clr
  Register #(.width(32)) register_4 (.D(D), .en(demultiplexer_1_out3), .clk(CLK), .Q(register_4_q));  // open: clr
  Register #(.width(32)) register_5 (.D(D), .en(demultiplexer_1_out4), .clk(CLK), .Q(register_5_q));  // open: clr
  Register #(.width(32)) register_6 (.D(D), .en(demultiplexer_1_out5), .clk(CLK), .Q(register_6_q));  // open: clr
  Register #(.width(32)) register_7 (.D(D), .en(demultiplexer_1_out6), .clk(CLK), .Q(register_7_q));  // open: clr
  Register #(.width(32)) register_8 (.D(D), .en(demultiplexer_1_out7), .clk(CLK), .Q(register_8_q));  // open: clr
  Register #(.width(32)) register_9 (.D(D), .en(demultiplexer_1_out8), .clk(CLK), .Q(register_9_q));  // open: clr
  Register #(.width(32)) register_10 (.D(D), .en(demultiplexer_1_out9), .clk(CLK), .Q(register_10_q));  // open: clr
  Register #(.width(32)) register_11 (.D(D), .en(demultiplexer_1_out10), .clk(CLK), .Q(register_11_q));  // open: clr
  Register #(.width(32)) register_12 (.D(D), .en(demultiplexer_1_out11), .clk(CLK), .Q(register_12_q));  // open: clr
  Register #(.width(32)) register_13 (.D(D), .en(demultiplexer_1_out12), .clk(CLK), .Q(register_13_q));  // open: clr
  Register #(.width(32)) register_14 (.D(D), .en(demultiplexer_1_out13), .clk(CLK), .Q(register_14_q));  // open: clr
  Register #(.width(32)) register_15 (.D(D), .en(demultiplexer_1_out14), .clk(CLK), .Q(register_15_q));  // open: clr
  Register #(.width(32)) register_16 (.D(D), .en(demultiplexer_1_out15), .clk(CLK), .Q(register_16_q));  // open: clr
  Register #(.width(32)) register_17 (.D(D), .en(demultiplexer_1_out16), .clk(CLK), .Q(register_17_q));  // open: clr
  Register #(.width(32)) register_18 (.D(D), .en(demultiplexer_1_out17), .clk(CLK), .Q(register_18_q));  // open: clr
  Register #(.width(32)) register_19 (.D(D), .en(demultiplexer_1_out18), .clk(CLK), .Q(register_19_q));  // open: clr
  Register #(.width(32)) register_20 (.D(D), .en(demultiplexer_1_out19), .clk(CLK), .Q(register_20_q));  // open: clr
  Register #(.width(32)) register_21 (.D(D), .en(demultiplexer_1_out20), .clk(CLK), .Q(register_21_q));  // open: clr
  Register #(.width(32)) register_22 (.D(D), .en(demultiplexer_1_out21), .clk(CLK), .Q(register_22_q));  // open: clr
  Register #(.width(32)) register_23 (.D(D), .en(demultiplexer_1_out22), .clk(CLK), .Q(register_23_q));  // open: clr
  Register #(.width(32)) register_24 (.D(D), .en(demultiplexer_1_out23), .clk(CLK), .Q(register_24_q));  // open: clr
  Register #(.width(32)) register_25 (.D(D), .en(demultiplexer_1_out24), .clk(CLK), .Q(register_25_q));  // open: clr
  Register #(.width(32)) register_26 (.D(D), .en(demultiplexer_1_out25), .clk(CLK), .Q(register_26_q));  // open: clr
  Register #(.width(32)) register_27 (.D(D), .en(demultiplexer_1_out26), .clk(CLK), .Q(register_27_q));  // open: clr
  Register #(.width(32)) register_28 (.D(D), .en(demultiplexer_1_out27), .clk(CLK), .Q(register_28_q));  // open: clr
  Register #(.width(32)) register_29 (.D(D), .en(demultiplexer_1_out28), .clk(CLK), .Q(register_29_q));  // open: clr
  Register #(.width(32)) register_30 (.D(D), .en(demultiplexer_1_out29), .clk(CLK), .Q(register_30_q));  // open: clr
  Register #(.width(32)) register_31 (.D(D), .en(demultiplexer_1_out30), .clk(CLK), .Q(register_31_q));  // open: clr
  Register #(.width(32)) register_32 (.D(D), .en(demultiplexer_1_out31), .clk(CLK), .Q(register_32_q));  // open: clr
  Multiplexer #(.select(5), .width(32)) multiplexer_1 (
    .in0(register_1_q), .in1(register_2_q), .in2(register_3_q), .in3(register_4_q), .in4(register_5_q),
    .in5(register_6_q), .in6(register_7_q), .in7(register_8_q), .in8(register_9_q), .in9(register_10_q),
    .in10(register_11_q), .in11(register_12_q), .in12(register_13_q), .in13(register_14_q),
    .in14(register_15_q), .in15(register_16_q), .in16(register_17_q), .in17(register_18_q),
    .in18(register_19_q), .in19(register_20_q), .in20(register_21_q), .in21(register_22_q),
    .in22(register_23_q), .in23(register_24_q), .in24(register_25_q), .in25(register_26_q),
    .in26(register_27_q), .in27(register_28_q), .in28(register_29_q), .in29(register_30_q),
    .in30(register_31_q), .in31(register_32_q), .out(O1), .sel(RS1));
  Multiplexer #(.select(5), .width(32)) multiplexer_2 (
    .in0(register_1_q), .in1(register_2_q), .in2(register_3_q), .in3(register_4_q), .in4(register_5_q),
    .in5(register_6_q), .in6(register_7_q), .in7(register_8_q), .in8(register_9_q), .in9(register_10_q),
    .in10(register_11_q), .in11(register_12_q), .in12(register_13_q), .in13(register_14_q),
    .in14(register_15_q), .in15(register_16_q), .in16(register_17_q), .in17(register_18_q),
    .in18(register_19_q), .in19(register_20_q), .in20(register_21_q), .in21(register_22_q),
    .in22(register_23_q), .in23(register_24_q), .in24(register_25_q), .in25(register_26_q),
    .in26(register_27_q), .in27(register_28_q), .in28(register_29_q), .in29(register_30_q),
    .in30(register_31_q), .in31(register_32_q), .out(O2), .sel(RS2));
endmodule

module ULA (
  input  [3:0] OPR,
  input  [31:0] OP1,
  input  [31:0] OP2,
  output [31:0] RES
);

  wire comparator_1_gt;
  wire [31:0] ADD, ANDx, DIV, EQ, GE, LT, MODx, MUL, ORx, SLLx, SRAx, SRLx, SUB, XORx;

  Adder #(.width(32)) adder_1 (.a(OP1), .b(OP2), .out(ADD));  // open: cin, cout
  Subtractor #(.width(32)) subtractor_1 (.a(OP1), .b(OP2), .out(SUB));  // open: bin, bout
  Divider #(.mode("twosComplement"), .width(32)) divider_1 (.a(OP1), .b(OP2), .out(DIV), .rem(MODx));  // open: upper
  Multiplier #(.mode("twosComplement"), .width(32)) multiplier_1 (.a(OP1), .b(OP2), .out(MUL));  // open: cin, cout
  assign ANDx = OP1 & OP2;  // AND_Gate and_1, 32 bits wide
  assign ORx = OP1 | OP2;  // OR_Gate or_1, 32 bits wide
  assign XORx = OP1 ^ OP2;  // XOR_Gate xor_1, 32 bits wide
  Shifter #(.width(32)) shifter_1 (.in(OP1), .\dist (OP2[4:0]), .out(SLLx));
  Shifter #(.shift("lr"), .width(32)) shifter_2 (.in(OP1), .\dist (OP2[4:0]), .out(SRLx));
  Shifter #(.shift("ar"), .width(32)) shifter_3 (.in(OP1), .\dist (OP2[4:0]), .out(SRAx));
  Comparator #(.width(32)) comparator_1 (.a(OP1), .b(OP2), .gt(comparator_1_gt), .eq(EQ[0]), .lt(LT[0]));
  and and_2 (GE[0], comparator_1_gt, EQ[0]);
  Multiplexer #(.select(4), .width(32)) multiplexer_1 (
    .in0(ADD), .in1(SUB), .in2(DIV), .in3(MODx), .in4(MUL), .in5(ANDx), .in6(ORx), .in7(XORx), .in8(SLLx),
    .in9(SRLx), .in10(SRAx), .in11(EQ), .in12(GE), .in13(LT), .out(RES), .sel(OPR));  // open: in14, in15
endmodule

module AND32 (
  input  [31:0] OP1,
  input  [31:0] OP2,
  output [31:0] RES
);

  and and_1 (RES[0], OP1[0], OP2[0]);
  and and_2 (RES[1], OP1[1], OP2[1]);
  and and_3 (RES[2], OP1[2], OP2[2]);
  and and_4 (RES[3], OP1[3], OP2[3]);
  and and_5 (RES[4], OP1[4], OP2[4]);
  and and_6 (RES[5], OP1[5], OP2[5]);
  and and_7 (RES[6], OP1[6], OP2[6]);
  and and_8 (RES[7], OP1[7], OP2[7]);
  and and_9 (RES[8], OP1[8], OP2[8]);
  and and_10 (RES[9], OP1[9], OP2[9]);
  and and_11 (RES[10], OP1[10], OP2[10]);
  and and_12 (RES[11], OP1[11], OP2[11]);
  and and_13 (RES[12], OP1[12], OP2[12]);
  and and_14 (RES[13], OP1[13], OP2[13]);
  and and_15 (RES[14], OP1[14], OP2[14]);
  and and_16 (RES[15], OP1[15], OP2[15]);
  and and_17 (RES[16], OP1[16], OP2[16]);
  and and_18 (RES[17], OP1[17], OP2[17]);
  and and_19 (RES[18], OP1[18], OP2[18]);
  and and_20 (RES[19], OP1[19], OP2[19]);
  and and_21 (RES[20], OP1[20], OP2[20]);
  and and_22 (RES[21], OP1[21], OP2[21]);
  and and_23 (RES[22], OP1[22], OP2[22]);
  and and_24 (RES[23], OP1[23], OP2[23]);
  and and_25 (RES[24], OP1[24], OP2[24]);
  and and_26 (RES[25], OP1[25], OP2[25]);
  and and_27 (RES[26], OP1[26], OP2[26]);
  and and_28 (RES[27], OP1[27], OP2[27]);
  and and_29 (RES[28], OP1[28], OP2[28]);
  and and_30 (RES[29], OP1[29], OP2[29]);
  and and_31 (RES[30], OP1[30], OP2[30]);
  and and_32 (RES[31], OP1[31], OP2[31]);
endmodule

module OR32 (
  input  [31:0] OP1,
  input  [31:0] OP2,
  output [31:0] RES
);

  or or_1 (RES[0], OP1[0], OP2[0]);
  or or_2 (RES[1], OP1[1], OP2[1]);
  or or_3 (RES[2], OP1[2], OP2[2]);
  or or_4 (RES[3], OP1[3], OP2[3]);
  or or_5 (RES[4], OP1[4], OP2[4]);
  or or_6 (RES[5], OP1[5], OP2[5]);
  or or_7 (RES[6], OP1[6], OP2[6]);
  or or_8 (RES[7], OP1[7], OP2[7]);
  or or_9 (RES[8], OP1[8], OP2[8]);
  or or_10 (RES[9], OP1[9], OP2[9]);
  or or_11 (RES[10], OP1[10], OP2[10]);
  or or_12 (RES[11], OP1[11], OP2[11]);
  or or_13 (RES[12], OP1[12], OP2[12]);
  or or_14 (RES[13], OP1[13], OP2[13]);
  or or_15 (RES[14], OP1[14], OP2[14]);
  or or_16 (RES[15], OP1[15], OP2[15]);
  or or_17 (RES[16], OP1[16], OP2[16]);
  or or_18 (RES[17], OP1[17], OP2[17]);
  or or_19 (RES[18], OP1[18], OP2[18]);
  or or_20 (RES[19], OP1[19], OP2[19]);
  or or_21 (RES[20], OP1[20], OP2[20]);
  or or_22 (RES[21], OP1[21], OP2[21]);
  or or_23 (RES[22], OP1[22], OP2[22]);
  or or_24 (RES[23], OP1[23], OP2[23]);
  or or_25 (RES[24], OP1[24], OP2[24]);
  or or_26 (RES[25], OP1[25], OP2[25]);
  or or_27 (RES[26], OP1[26], OP2[26]);
  or or_28 (RES[27], OP1[27], OP2[27]);
  or or_29 (RES[28], OP1[28], OP2[28]);
  or or_30 (RES[29], OP1[29], OP2[29]);
  or or_31 (RES[30], OP1[30], OP2[30]);
  or or_32 (RES[31], OP1[31], OP2[31]);
endmodule

module XOR32 (
  input  [31:0] OP1,
  input  [31:0] OP2,
  output [31:0] RES
);

  xor xor_1 (RES[0], OP1[0], OP2[0]);
  xor xor_2 (RES[1], OP1[1], OP2[1]);
  xor xor_3 (RES[2], OP1[2], OP2[2]);
  xor xor_4 (RES[3], OP1[3], OP2[3]);
  xor xor_5 (RES[4], OP1[4], OP2[4]);
  xor xor_6 (RES[5], OP1[5], OP2[5]);
  xor xor_7 (RES[6], OP1[6], OP2[6]);
  xor xor_8 (RES[7], OP1[7], OP2[7]);
  xor xor_9 (RES[8], OP1[8], OP2[8]);
  xor xor_10 (RES[9], OP1[9], OP2[9]);
  xor xor_11 (RES[10], OP1[10], OP2[10]);
  xor xor_12 (RES[11], OP1[11], OP2[11]);
  xor xor_13 (RES[12], OP1[12], OP2[12]);
  xor xor_14 (RES[13], OP1[13], OP2[13]);
  xor xor_15 (RES[14], OP1[14], OP2[14]);
  xor xor_16 (RES[15], OP1[15], OP2[15]);
  xor xor_17 (RES[16], OP1[16], OP2[16]);
  xor xor_18 (RES[17], OP1[17], OP2[17]);
  xor xor_19 (RES[18], OP1[18], OP2[18]);
  xor xor_20 (RES[19], OP1[19], OP2[19]);
  xor xor_21 (RES[20], OP1[20], OP2[20]);
  xor xor_22 (RES[21], OP1[21], OP2[21]);
  xor xor_23 (RES[22], OP1[22], OP2[22]);
  xor xor_24 (RES[23], OP1[23], OP2[23]);
  xor xor_25 (RES[24], OP1[24], OP2[24]);
  xor xor_26 (RES[25], OP1[25], OP2[25]);
  xor xor_27 (RES[26], OP1[26], OP2[26]);
  xor xor_28 (RES[27], OP1[27], OP2[27]);
  xor xor_29 (RES[28], OP1[28], OP2[28]);
  xor xor_30 (RES[29], OP1[29], OP2[29]);
  xor xor_31 (RES[30], OP1[30], OP2[30]);
  xor xor_32 (RES[31], OP1[31], OP2[31]);
endmodule
